# Fritzing sketch Gary the Gonk (saved by Fritzing 1.0.3b)

parts:
  Mod1 = Raspberry Pi Pico
  J1 = Basic Servo
  M1 = fc-51 [package=THT]

nets:
  N1: Mod1.pin_21, J1.pulse
  N2: Mod1.pin_22, M1.pin1
  N3: Mod1.pin_33, Mod1.pin_38, M1.pin2
  N4: Mod1.pin_40, M1.pin3

custom parts:
  Raspberry Pi Pico: Raspberry Pi Pico. Based around the RP2040 microcontroller the Pico is a low cost microcontroller device bringing Raspberry Pi quality, cost, and easy of use to the microcontroller space. Jan 2021, Split part in to two versions: tht (this one) and SMD. This one will drill holes for a .1 in header in pcb to allow plugging in the module as well as providing pads to solder the module to the top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
